// Logisim project 231project.circ as structural Verilog: 9 circuits, main circuit main
module main (
  input  in_1,
  input  in_2,
  input  in_3,
  output A,
  output B,
  output C,
  output D,
  output E,
  output F,
  output G
);

  wire n7404_1_pin2, n7404_1_pin4, n7404_1_pin6, n7411_1_pin6, n7411_1_pin7, n7411_1_pin8, n7411_1_pin12,
       n7411_1_pin14, n7411_2_pin6, n7411_2_pin7, n7411_2_pin8, n7411_2_pin12, n7411_2_pin14, n7411_3_pin6,
       n7411_3_pin7, n7411_3_pin12, n7411_3_pin14, n7432_1_pin3, n7432_1_pin7, n7432_1_pin8, n7432_1_pin14,
       n7432_2_pin3, n7432_2_pin6, n7432_2_pin7, n7432_2_pin14;

  _7404 #(.ShowInternalStructure("true"), .VccGndPorts("true")) u_7404_1 (
    .pin1(in_1), .pin2(n7404_1_pin2), .pin3(in_2), .pin4(n7404_1_pin4), .pin5(in_3), .pin6(n7404_1_pin6));  // open: pin7, pin14, pin13, pin12, pin11, pin10, pin9, pin8
  _7411 #(.ShowInternalStructure("true"), .VccGndPorts("true")) u_7411_1 (
    .pin1(n7404_1_pin2), .pin2(n7404_1_pin4), .pin3(n7404_1_pin2), .pin4(n7404_1_pin4), .pin5(in_3),
    .pin6(n7411_1_pin6), .pin7(n7411_1_pin7), .pin14(n7411_1_pin14), .pin13(n7404_1_pin6),
    .pin12(n7411_1_pin12), .pin11(n7404_1_pin2), .pin10(in_2), .pin9(n7404_1_pin6), .pin8(n7411_1_pin8));
  _7411 #(.ShowInternalStructure("true"), .VccGndPorts("true")) u_7411_2 (
    .pin1(n7404_1_pin2), .pin2(in_2), .pin3(in_1), .pin4(n7404_1_pin4), .pin5(n7404_1_pin6),
    .pin6(n7411_2_pin6), .pin7(n7411_2_pin7), .pin14(n7411_2_pin14), .pin13(in_3), .pin12(n7411_2_pin12),
    .pin11(in_1), .pin10(n7404_1_pin4), .pin9(in_3), .pin8(n7411_2_pin8));
  _7411 #(.ShowInternalStructure("true"), .VccGndPorts("true")) u_7411_3 (
    .pin1(in_1), .pin2(in_2), .pin3(in_1), .pin4(in_2), .pin5(in_3), .pin6(n7411_3_pin6),
    .pin7(n7411_3_pin7), .pin14(n7411_3_pin14), .pin13(n7404_1_pin6), .pin12(n7411_3_pin12));  // open: pin11, pin10, pin9, pin8
  _7432 #(.ShowInternalStructure("true"), .VccGndPorts("true")) u_7432_1 (
    .pin1(n7411_1_pin12), .pin2(n7411_1_pin6), .pin3(n7432_1_pin3), .pin4(n7411_1_pin8),
    .pin5(n7411_2_pin12), .pin7(n7432_1_pin7), .pin14(n7432_1_pin14), .pin13(n7411_2_pin6),
    .pin12(n7411_2_pin8), .pin10(n7411_3_pin12), .pin9(n7411_3_pin6), .pin8(n7432_1_pin8));  // open: pin6, pin11
  _7432 #(.ShowInternalStructure("true"), .VccGndPorts("true")) u_7432_2 (
    .pin1(n7432_1_pin3), .pin2(n7411_1_pin8), .pin3(n7432_2_pin3), .pin4(n7432_2_pin3), .pin5(n7411_2_pin6),
    .pin6(n7432_2_pin6), .pin7(n7432_2_pin7), .pin14(n7432_2_pin14), .pin10(n7432_2_pin6),
    .pin9(n7432_1_pin8), .pin8(A));  // open: pin13, pin12, pin11
  _7_Segment_Display u_7_segment_display_1 (.a(A));  // open: g, f, b, e, d, c, dp
  // also tied to GND on the sheet: {n7411_1_pin7, n7411_2_pin7, n7411_3_pin7, n7432_1_pin7, n7432_2_pin7}
  // also tied to VCC on the sheet: {n7411_2_pin14, n7411_1_pin14, n7411_3_pin14, n7432_1_pin14, n7432_2_pin14}

  // Notes on the sheet:
  //   X
  //   Y
  //   Z
  //   X'
  //   Y'
  //   Z'
  //   1
  //   4
  //   7
  //   0
  //   2
  //   3
  //   5
  //   6
endmodule

module SOM_circuit (
  input  X,
  input  Y,
  input  Z,
  output A,
  output B,
  output C,
  output D,
  output E,
  output F,
  output G
);

  wire and_1_out, and_2_out, and_3_out, and_4_out, and_5_out, and_6_out, and_7_out, and_8_out, and_9_out,
       and_10_out, and_11_out, and_12_out, and_13_out, and_14_out, and_15_out, and_16_out, and_17_out,
       and_18_out, and_19_out, and_20_out, and_21_out, and_22_out, and_23_out, and_24_out, and_25_out,
       and_26_out, and_27_out, and_28_out, and_29_out, and_30_out, and_31_out, and_32_out, and_33_out,
       and_34_out, not_1_out, not_2_out, not_3_out;

  not not_1 (not_1_out, X);
  not not_2 (not_2_out, Y);
  not not_3 (not_3_out, Z);
  and and_1 (and_1_out, not_1_out, not_2_out, not_3_out);
  and and_2 (and_2_out, not_1_out, not_2_out, Z);
  and and_3 (and_3_out, not_1_out, Y, not_3_out);
  and and_4 (and_4_out, X, not_2_out, not_3_out);
  and and_5 (and_5_out, X, Y, not_3_out);
  and and_6 (and_6_out, X, Y, Z);
  and and_7 (and_7_out, not_1_out, not_2_out, Z);
  and and_8 (and_8_out, X, not_2_out, not_3_out);
  and and_9 (and_9_out, X, not_2_out, Z);
  and and_10 (and_10_out, X, Y, not_3_out);
  and and_11 (and_11_out, X, Y, Z);
  and and_12 (and_12_out, not_1_out, not_2_out, Z);
  and and_13 (and_13_out, X, not_2_out, not_3_out);
  and and_14 (and_14_out, X, not_2_out, Z);
  and and_15 (and_15_out, X, Y, not_3_out);
  and and_16 (and_16_out, X, Y, Z);
  and and_17 (and_17_out, not_1_out, not_2_out, not_3_out);
  and and_18 (and_18_out, not_1_out, not_2_out, Z);
  and and_19 (and_19_out, not_1_out, Y, not_3_out);
  and and_20 (and_20_out, not_1_out, Y, Z);
  and and_21 (and_21_out, X, not_2_out, not_3_out);
  and and_22 (and_22_out, X, not_2_out, Z);
  and and_23 (and_23_out, X, Y, not_3_out);
  and and_24 (and_24_out, not_1_out, not_2_out, not_3_out);
  and and_25 (and_25_out, not_1_out, not_2_out, Z);
  and and_26 (and_26_out, not_1_out, Y, not_3_out);
  and and_27 (and_27_out, not_1_out, Y, Z);
  and and_28 (and_28_out, X, not_2_out, not_3_out);
  and and_29 (and_29_out, X, not_2_out, Z);
  and and_30 (and_30_out, X, Y, not_3_out);
  and and_31 (and_31_out, not_1_out, not_2_out, Z);
  and and_32 (and_32_out, not_1_out, Y, not_3_out);
  and and_33 (and_33_out, X, not_2_out, Z);
  and and_34 (and_34_out, X, Y, not_3_out);
  or or_1 (B, and_7_out, and_8_out, and_9_out, and_10_out, and_11_out);
  or or_2 (C, and_12_out, and_13_out, and_14_out, and_15_out, and_16_out);
  or or_3 (G, and_31_out, and_32_out, and_33_out, and_34_out);
  or or_4 (A, and_1_out, and_2_out, and_3_out, and_4_out, and_5_out, and_6_out);
  or or_5 (E, and_17_out, and_18_out, and_19_out, and_20_out, and_21_out, and_22_out, and_23_out);
  or or_6 (F, and_24_out, and_25_out, and_26_out, and_27_out, and_28_out, and_29_out, and_30_out);
  _7_Segment_Display u_7_segment_display_1 (.g(G), .f(F), .a(A), .b(B), .e(E), .d(1'b0), .c(C), .dp(1'b0));

  assign D = 1'b0;

  // Notes on the sheet:
  //   Fig: Sum Of Minterms (SOM)
endmodule

module POM_circuit (
  input  X,
  input  Y,
  input  Z,
  output A,
  output B,
  output C,
  output D,
  output E,
  output F,
  output G
);

  wire not_1_out, not_2_out, not_3_out, or_1_out, or_2_out, or_3_out, or_4_out, or_5_out, or_6_out, or_7_out,
       or_8_out, or_9_out, or_10_out, or_11_out, or_12_out, or_13_out, or_14_out, or_15_out, or_16_out,
       or_19_out, or_20_out, or_21_out, or_22_out;

  not not_1 (not_1_out, X);
  not not_2 (not_2_out, Y);
  not not_3 (not_3_out, Z);
  or or_1 (or_1_out, X, not_2_out, not_3_out);
  or or_2 (or_2_out, not_1_out, Y, not_3_out);
  or or_3 (or_3_out, X, Y, Z);
  or or_4 (or_4_out, X, not_2_out, Z);
  or or_5 (or_5_out, X, not_2_out, not_3_out);
  or or_6 (or_6_out, X, Y, Z);
  or or_7 (or_7_out, X, not_2_out, Z);
  or or_8 (or_8_out, X, not_2_out, not_3_out);
  or or_9 (or_9_out, X, Y, Z);
  or or_10 (or_10_out, X, Y, not_3_out);
  or or_11 (or_11_out, X, not_2_out, Z);
  or or_12 (or_12_out, X, not_2_out, not_3_out);
  or or_13 (or_13_out, not_1_out, Y, Z);
  or or_14 (or_14_out, not_1_out, Y, not_3_out);
  or or_15 (or_15_out, not_1_out, not_2_out, Z);
  or or_16 (or_16_out, not_1_out, not_2_out, not_3_out);
  or or_17 (E, not_1_out, not_2_out, not_3_out);
  or or_18 (F, not_1_out, not_2_out, not_3_out);
  or or_19 (or_19_out, X, Y, Z);
  or or_20 (or_20_out, X, not_2_out, not_3_out);
  or or_21 (or_21_out, not_1_out, Y, Z);
  or or_22 (or_22_out, not_1_out, not_2_out, not_3_out);
  and and_1 (A, or_1_out, or_2_out);
  and and_2 (B, or_3_out, or_4_out, or_5_out);
  and and_3 (C, or_6_out, or_7_out, or_8_out);
  and and_4 (D, or_9_out, or_10_out, or_11_out, or_12_out, or_13_out, or_14_out, or_15_out, or_16_out);
  and and_5 (G, or_19_out, or_20_out, or_21_out, or_22_out);
  _7_Segment_Display u_7_segment_display_1 (.g(G), .f(F), .a(A), .b(B), .e(E), .d(D), .c(C), .dp(1'b0));

  // Notes on the sheet:
  //   Fig: Product of Maxterms (POM)
endmodule

module SOP_circuit (
  input  X,
  input  Y,
  input  Z,
  output A,
  output B,
  output C,
  output D,
  output E,
  output F,
  output G
);

  wire and_1_out, and_2_out, and_3_out, and_4_out, and_5_out, and_6_out, and_7_out, and_8_out, not_1_out,
       not_2_out, not_3_out;

  not not_1 (not_1_out, X);
  not not_2 (not_2_out, Y);
  not not_3 (not_3_out, Z);
  and and_1 (and_1_out, not_1_out, not_2_out);
  and and_2 (and_2_out, X, Y);
  and and_3 (and_3_out, not_2_out, Z);
  and and_4 (and_4_out, not_2_out, Z);
  and and_5 (and_5_out, Y, not_3_out);
  and and_6 (and_6_out, Y, not_3_out);
  and and_7 (and_7_out, not_2_out, Z);
  and and_8 (and_8_out, Y, not_3_out);
  or or_1 (A, and_1_out, not_3_out, and_2_out);
  or or_2 (B, and_3_out, X);
  or or_3 (C, and_4_out, X);
  or or_4 (E, not_1_out, not_2_out, and_5_out);
  or or_5 (F, not_1_out, not_2_out, and_6_out);
  or or_6 (G, and_7_out, and_8_out);
  _7_Segment_Display u_7_segment_display_1 (.g(G), .f(F), .a(A), .b(B), .e(E), .d(1'b0), .c(C), .dp(1'b0));

  assign D = 1'b0;

  // Notes on the sheet:
  //   Fig: Sum of Product (SOP) circuit
endmodule

module POS_circuit (
  input  X,
  input  Y,
  input  Z,
  output A,
  output B,
  output C,
  output D,
  output E,
  output F,
  output G
);

  wire not_1_out, not_2_out, not_3_out, or_1_out, or_2_out, or_3_out, or_4_out, or_5_out, or_6_out, or_9_out,
       or_10_out;

  not not_1 (not_1_out, X);
  not not_2 (not_2_out, Y);
  not not_3 (not_3_out, Z);
  or or_1 (or_1_out, X, not_2_out, not_3_out);
  or or_2 (or_2_out, not_1_out, Y, not_3_out);
  or or_3 (or_3_out, X, not_2_out);
  or or_4 (or_4_out, X, Z);
  or or_5 (or_5_out, X, not_2_out);
  or or_6 (or_6_out, X, Z);
  or or_7 (E, not_1_out, not_2_out, not_3_out);
  or or_8 (F, not_1_out, not_2_out, not_3_out);
  or or_9 (or_9_out, Y, Z);
  or or_10 (or_10_out, not_2_out, not_3_out);
  and and_1 (A, or_1_out, or_2_out);
  and and_2 (B, or_3_out, or_4_out);
  and and_3 (C, or_5_out, or_6_out);
  and and_4 (G, or_9_out, or_10_out);
  _7_Segment_Display u_7_segment_display_1 (.g(G), .f(F), .a(A), .b(B), .e(E), .d(1'b0), .c(C), .dp(1'b0));

  assign D = 1'b0;

  // Notes on the sheet:
  //   Fig: Product of sum (POS) circuit
endmodule

module NAND_gate_format (
  input  X,
  input  Y,
  input  Z,
  output A,
  output B,
  output C,
  output D,
  output E,
  output F,
  output G
);

  wire nand_1_out, nand_2_out, nand_3_out, nand_4_out, nand_5_out, nand_6_out, nand_7_out, nand_8_out,
       nand_9_out, nand_10_out, nand_11_out;

  nand nand_1 (nand_1_out, 1'b1, X);
  nand nand_2 (nand_2_out, 1'b1, Y);
  nand nand_3 (nand_3_out, 1'b1, Z);
  nand nand_4 (nand_4_out, X, Y);
  nand nand_5 (nand_5_out, nand_1_out, nand_2_out);
  nand nand_6 (nand_6_out, nand_2_out, Z);
  nand nand_7 (nand_7_out, nand_2_out, Z);
  nand nand_8 (nand_8_out, Y, nand_3_out);
  nand nand_9 (nand_9_out, Y, nand_3_out);
  nand nand_10 (nand_10_out, nand_2_out, Z);
  nand nand_11 (nand_11_out, Y, nand_3_out);
  nand nand_12 (A, nand_4_out, nand_5_out, Z);
  nand nand_13 (B, nand_1_out, nand_6_out);
  nand nand_14 (C, nand_1_out, nand_7_out);
  nand nand_15 (E, X, Y, nand_8_out);
  nand nand_16 (F, X, Y, nand_9_out);
  nand nand_17 (G, nand_10_out, nand_11_out);
  _7_Segment_Display u_7_segment_display_1 (.g(G), .f(F), .a(A), .b(B), .e(E), .d(1'b0), .c(C), .dp(1'b0));

  assign D = 1'b0;

  // Notes on the sheet:
  //   Fig: NAND Gate format equation circuit diagram
endmodule

module NOR_gate_format (
  input  X,
  input  Y,
  input  Z,
  output A,
  output B,
  output C,
  output D,
  output E,
  output F,
  output G
);

  wire nor_1_out, nor_2_out, nor_3_out, nor_4_out, nor_5_out, nor_6_out, nor_7_out, nor_8_out, nor_9_out,
       nor_10_out, nor_11_out, nor_12_out, nor_13_out;

  nor nor_1 (nor_1_out, 1'b1, X);
  nor nor_2 (nor_2_out, 1'b1, Y);
  nor nor_3 (nor_3_out, 1'b1, Z);
  nor nor_4 (nor_4_out, nor_1_out, Y, nor_3_out);
  nor nor_5 (nor_5_out, X, nor_2_out, nor_3_out);
  nor nor_6 (nor_6_out, X, nor_2_out);
  nor nor_7 (nor_7_out, X, Z);
  nor nor_8 (nor_8_out, X, nor_2_out);
  nor nor_9 (nor_9_out, X, Z);
  nor nor_10 (nor_10_out, nor_1_out, nor_2_out, nor_3_out);
  nor nor_11 (nor_11_out, nor_3_out, nor_2_out, nor_1_out);
  nor nor_12 (nor_12_out, Y, Z);
  nor nor_13 (nor_13_out, nor_2_out, nor_3_out);
  nor nor_14 (A, nor_4_out, nor_5_out);
  nor nor_15 (E, nor_10_out, nor_10_out);
  nor nor_16 (F, nor_11_out, nor_11_out);
  nor nor_17 (G, nor_12_out, nor_13_out);
  nor nor_18 (B, nor_6_out, nor_7_out);
  nor nor_19 (C, nor_8_out, nor_9_out);
  _7_Segment_Display u_7_segment_display_1 (.g(G), .f(F), .a(A), .b(B), .e(E), .d(1'b0), .c(C), .dp(1'b0));

  assign D = 1'b0;

  // Notes on the sheet:
  //   A
  //   B
  //   C
  //   E
  //   F
  //   Fig: NOR Gate format equation circuit diagram
endmodule

module MUX_format_circuit (
  input  X,
  input  Y,
  input  Z,
  output A,
  output B,
  output C,
  output D,
  output E,
  output F,
  output G
);

  wire n7404_1_pin7, n7404_1_pin12, n7404_1_pin14, n74153_1_pin1, n74153_1_pin3, n74153_2_pin1,
       n74153_2_pin3, n74153_3_pin1, n74153_3_pin4;

  _7404 #(.ShowInternalStructure("true"), .VccGndPorts("true")) u_7404_1 (
    .pin7(n7404_1_pin7), .pin14(n7404_1_pin14), .pin13(Z), .pin12(n7404_1_pin12));  // open: pin1, pin2, pin3, pin4, pin5, pin6, pin11, pin10, pin9, pin8
  _74153 #(.ShowInternalStructure("true"), .VccGndPorts("true")) u_74153_1 (
    .pin1(n74153_1_pin1), .pin2(Y), .pin3(n74153_1_pin3), .pin4(n7404_1_pin12), .pin5(n7404_1_pin12),
    .pin6(n74153_1_pin3), .pin7(A), .pin8(n74153_1_pin1), .pin16(n74153_1_pin3), .pin15(n74153_1_pin1),
    .pin14(X), .pin13(n74153_1_pin3), .pin12(n74153_1_pin3), .pin11(n74153_1_pin1), .pin10(Z), .pin9(B));
  _74153 #(.ShowInternalStructure("true"), .VccGndPorts("true")) u_74153_2 (
    .pin1(n74153_2_pin1), .pin2(Y), .pin3(n74153_2_pin3), .pin4(n74153_2_pin3), .pin5(n74153_2_pin1),
    .pin6(Z), .pin7(C), .pin8(n74153_2_pin1), .pin16(n74153_2_pin3), .pin15(n74153_2_pin1), .pin14(X),
    .pin13(n7404_1_pin12), .pin12(n74153_2_pin3), .pin11(n74153_2_pin3), .pin10(n74153_2_pin3), .pin9(E));
  _74153 #(.ShowInternalStructure("true"), .VccGndPorts("true")) u_74153_3 (
    .pin1(n74153_3_pin1), .pin2(Y), .pin3(n7404_1_pin12), .pin4(n74153_3_pin4), .pin5(n74153_3_pin4),
    .pin6(n74153_3_pin4), .pin7(F), .pin8(n74153_3_pin1), .pin16(n74153_3_pin4), .pin15(n74153_3_pin1),
    .pin14(X), .pin13(n7404_1_pin12), .pin12(Z), .pin11(n7404_1_pin12), .pin10(Z), .pin9(G));
  _7_Segment_Display u_7_segment_display_1 (.g(G), .f(F), .a(A), .b(B), .e(E), .d(1'b0), .c(C), .dp(1'b0));

  assign D = 1'b0;
  // also tied to GND on the sheet: {n7404_1_pin7, n74153_2_pin1, n74153_3_pin1, n74153_1_pin1}
  // also tied to VCC on the sheet: {n7404_1_pin14, n74153_3_pin4, n74153_2_pin3, n74153_1_pin3}

  // Notes on the sheet:
  //   A
  //   C
  //   F
  //   B
  //   E
  //   G
  //   Fig: 4:1 MUX format circuit
endmodule

module Decoder_format_circuit (
  input  X,
  input  Y,
  input  Z
);

  wire and_1_out, and_2_out, and_3_out, and_4_out, and_5_out, and_6_out, n74138_1_pin4, n74138_1_pin6,
       n74138_1_pin7, n74138_1_pin9, n74138_1_pin10, n74138_1_pin11, n74138_1_pin12, n74138_1_pin13,
       n74138_1_pin14, n74138_1_pin15;

  _74138 #(.ShowInternalStructure("true"), .VccGndPorts("true")) u_74138_1 (
    .pin1(X), .pin2(Y), .pin3(Z), .pin4(n74138_1_pin4), .pin5(n74138_1_pin4), .pin6(n74138_1_pin6),
    .pin7(n74138_1_pin7), .pin8(n74138_1_pin4), .pin16(n74138_1_pin6), .pin15(n74138_1_pin15),
    .pin14(n74138_1_pin14), .pin13(n74138_1_pin13), .pin12(n74138_1_pin12), .pin11(n74138_1_pin11),
    .pin10(n74138_1_pin10), .pin9(n74138_1_pin9));
  and and_1 (and_1_out, n74138_1_pin12, n74138_1_pin10);
  and and_2 (and_2_out, n74138_1_pin15, n74138_1_pin13, n74138_1_pin12);
  and and_3 (and_3_out, n74138_1_pin15, n74138_1_pin14, n74138_1_pin13);
  and and_4 (and_4_out, n74138_1_pin12, n74138_1_pin11, n74138_1_pin10);
  and and_5 (and_5_out, and_3_out, and_4_out, n74138_1_pin7, n74138_1_pin9);
  and and_6 (and_6_out, n74138_1_pin15, n74138_1_pin12, n74138_1_pin11, n74138_1_pin7);
  _7_Segment_Display u_7_segment_display_1 (
    .g(and_6_out), .f(n74138_1_pin7), .a(and_1_out), .b(and_2_out), .e(n74138_1_pin7), .d(and_5_out),
    .c(and_2_out));  // open: dp
  // also tied to GND on the sheet: n74138_1_pin4
  // also tied to VCC on the sheet: n74138_1_pin6
endmodule
